// Logisim project alu.circ as structural Verilog: 2 circuits, main circuit alu
module alu (
  input  [31:0] A,
  input  [31:0] B,
  input  [3:0] ALUSel,
  output [31:0] ALUResult
);

  wire comparator_1_gt, comparator_1_lt, comparator_2_lt;
  wire [4:0] bit_extender_7_out, bit_extender_8_out, bit_extender_9_out, undriven_4;
  wire [31:0] add0, and7, and_1_out, and_2_out, bit_extender_1_out, bit_extender_2_out, mul8, mulh9, mulhu11,
       multiplier_4_out, or6, shifter_1_out, shifter_2_out, sll1, slt2, sra13, srl5, sub12, undriven,
       undriven_2, undriven_3, xor4;
  wire [63:0] bit_extender_3_out, bit_extender_4_out, bit_extender_5_out, bit_extender_6_out,
       multiplier_2_out, multiplier_3_out, shifter_6_out, shifter_7_out;

  Multiplexer #(.enable("false"), .select(4), .width(32)) multiplexer_1 (
    .in0(add0), .in1(sll1), .in2(slt2), .in3(undriven), .in4(xor4), .in5(srl5), .in6(or6), .in7(and7),
    .in8(mul8), .in9(mulh9), .in10(undriven_2), .in11(mulhu11), .in12(sub12), .in13(sra13),
    .in14(undriven_3), .in15(B), .out(ALUResult), .sel(ALUSel));
  Comparator #(.width(32)) comparator_1 (.a(B), .b(32'h20), .gt(comparator_1_gt), .lt(comparator_1_lt));  // open: eq
  Shifter #(.shift("ar"), .width(32)) shifter_1 (.in(A), .\dist (B[4:0]), .out(shifter_1_out));
  Shifter #(.shift("ar"), .width(32)) shifter_2 (.in(A), .\dist (undriven_4), .out(shifter_2_out));
  assign bit_extender_1_out = {{31{comparator_1_gt}}, comparator_1_gt};  // Bit_Extender bit_extender_1
  assign bit_extender_2_out = {{31{comparator_1_lt}}, comparator_1_lt};  // Bit_Extender bit_extender_2
  assign bit_extender_3_out = {{32{A[31]}}, A};  // Bit_Extender bit_extender_3
  assign bit_extender_4_out = {{32{B[31]}}, B};  // Bit_Extender bit_extender_4
  assign bit_extender_5_out = {{32{1'b0}}, A};  // Bit_Extender bit_extender_5
  assign bit_extender_6_out = {{32{1'b0}}, B};  // Bit_Extender bit_extender_6
  Shifter #(.shift("ar"), .width(32)) shifter_3 (.in(A));  // open: dist, out
  assign and_1_out = shifter_2_out & bit_extender_1_out;  // AND_Gate and_1, 32 bits wide
  assign and_2_out = bit_extender_2_out & shifter_1_out;  // AND_Gate and_2, 32 bits wide
  Adder #(.width(32)) adder_1 (.a(A), .b(B), .out(add0));  // open: cin, cout
  Bit_Extender #(.in_width(32), .out_width(5)) bit_extender_7 (.in(B), .out(bit_extender_7_out));
  Comparator #(.width(32)) comparator_2 (.a(A), .b(B), .lt(comparator_2_lt));  // open: gt, eq
  assign xor4 = A ^ B;  // XOR_Gate xor_1, 32 bits wide
  Bit_Extender #(.in_width(32), .out_width(5)) bit_extender_8 (.in(B), .out(bit_extender_8_out));
  assign or6 = A | B;  // OR_Gate or_1, 32 bits wide
  assign and7 = A & B;  // AND_Gate and_3, 32 bits wide
  Multiplier #(.mode("twosComplement"), .width(32)) multiplier_1 (.a(A), .b(B), .out(mul8));  // open: cin, cout
  Multiplier #(.mode("twosComplement"), .width(64)) multiplier_2 (
    .a(bit_extender_3_out), .b(bit_extender_4_out), .out(multiplier_2_out));  // open: cin, cout
  Multiplier #(.width(64)) multiplier_3 (
    .a(bit_extender_5_out), .b(bit_extender_6_out), .out(multiplier_3_out));  // open: cin, cout
  Adder #(.width(32)) adder_2 (.a(A), .b(multiplier_4_out), .out(sub12));  // open: cin, cout
  Multiplier #(.width(32)) multiplier_4 (.a({32{1'b1}}), .b(B), .out(multiplier_4_out));  // open: cin, cout
  Bit_Extender #(.in_width(32), .out_width(5)) bit_extender_9 (.in(B), .out(bit_extender_9_out));
  // OR_Gate or_2 has open pins: in0=and_1_out, in1=and_2_out, out=open
  Shifter #(.width(32)) shifter_4 (.in(A), .\dist (bit_extender_7_out), .out(sll1));
  assign slt2 = {{31{1'b0}}, comparator_2_lt};  // Bit_Extender bit_extender_10
  Shifter #(.shift("lr"), .width(32)) shifter_5 (.in(A), .\dist (bit_extender_8_out), .out(srl5));
  Shifter #(.shift("lr"), .width(64)) shifter_6 (.in(multiplier_2_out), .\dist (6'b100000), .out(shifter_6_out));
  Shifter #(.shift("lr"), .width(64)) shifter_7 (.in(multiplier_3_out), .\dist (6'b100000), .out(shifter_7_out));
  Shifter #(.shift("ar"), .width(32)) shifter_8 (.in(A), .\dist (bit_extender_9_out), .out(sra13));
  Bit_Extender #(.in_width(64), .out_width(32)) bit_extender_11 (.in(shifter_6_out), .out(mulh9));
  Bit_Extender #(.in_width(64), .out_width(32)) bit_extender_12 (.in(shifter_7_out), .out(mulhu11));

  // Other names for the same wires on the sheet: bsel15[31:0] = B

  // Notes on the sheet:
  //   INPUTS to your circuit
  //   DON'T CHANGE THE LOCATIONS OF THE INPUTS AND OUTPUTS!
  //   OUTPUT from your circuit
endmodule

module SRA_divisor (
  input  [31:0] B,
  output [31:0] B_divided
);

  wire comparator_1_eq, comparator_2_eq, comparator_2_gt, comparator_2_lt, comparator_3_lt, comparator_4_eq,
       comparator_4_lt, comparator_5_eq, comparator_5_gt, comparator_5_lt, or_1_out, or_2_out, or_3_out;
  wire [31:0] A, and_1_out, and_2_out, and_3_out, and_4_out, B_t, bit_extender_1_out, bit_extender_2_out,
       bit_extender_3_out, bit_extender_4_out, bit_extender_5_out, shifter_1_out, shifter_2_out,
       shifter_3_out, shifter_4_out;

  Shifter #(.shift("ar"), .width(32)) shifter_1 (.in(A), .\dist (B_t[4:0]), .out(shifter_1_out));
  Shifter #(.shift("lr"), .width(32)) shifter_2 (.in(B_t), .\dist (5'b00101), .out(shifter_2_out));
  Shifter #(.shift("lr"), .width(32)) shifter_3 (.in(B_t), .\dist (5'b00101), .out(shifter_3_out));
  Comparator #(.width(32)) comparator_1 (.b({32{1'b0}}), .eq(comparator_1_eq));  // open: a, gt, lt
  Shifter #(.shift("lr"), .width(32)) shifter_4 (.in(shifter_2_out), .\dist (5'b00101), .out(shifter_4_out));
  Comparator #(.width(32)) comparator_2 (
    .a(shifter_2_out), .b(32'h20), .gt(comparator_2_gt), .eq(comparator_2_eq), .lt(comparator_2_lt));
  Comparator #(.width(32)) comparator_3 (.a(shifter_3_out), .b(32'h20), .lt(comparator_3_lt));  // open: gt, eq
  // NOT_Gate not_1 has open pins: in=comparator_1_eq, out=open
  Comparator #(.width(32)) comparator_4 (
    .a(shifter_4_out), .b(32'h20), .eq(comparator_4_eq), .lt(comparator_4_lt));  // open: gt
  or or_1 (or_1_out, comparator_2_eq, comparator_2_lt);
  Comparator #(.width(32)) comparator_5 (
    .a(B_t), .b(32'h20), .gt(comparator_5_gt), .eq(comparator_5_eq), .lt(comparator_5_lt));
  assign bit_extender_1_out = {{31{comparator_2_gt}}, comparator_2_gt};  // Bit_Extender bit_extender_1
  assign bit_extender_2_out = {{31{or_1_out}}, or_1_out};  // Bit_Extender bit_extender_2
  assign bit_extender_3_out = {{31{comparator_5_gt}}, comparator_5_gt};  // Bit_Extender bit_extender_3
  or or_2 (or_2_out, comparator_4_eq, comparator_4_lt);
  assign and_1_out = bit_extender_2_out & shifter_2_out;  // AND_Gate and_1, 32 bits wide
  assign and_2_out = and_1_out & bit_extender_3_out;  // AND_Gate and_2, 32 bits wide
  assign bit_extender_4_out = {{31{or_3_out}}, or_3_out};  // Bit_Extender bit_extender_4
  or or_3 (or_3_out, comparator_5_eq, comparator_5_lt);
  assign bit_extender_5_out = {{31{or_2_out}}, or_2_out};  // Bit_Extender bit_extender_5
  assign and_3_out = bit_extender_5_out & shifter_4_out;  // AND_Gate and_3, 32 bits wide
  assign and_4_out = bit_extender_4_out & B;  // AND_Gate and_4, 32 bits wide
  // AND_Gate and_5 has open pins: in0=and_3_out, in1=bit_extender_1_out, out=open
  assign B_divided = and_2_out | and_4_out;  // OR_Gate or_4, 32 bits wide
endmodule
