// Logisim project branch-comp.circ as structural Verilog: 1 circuit, main circuit branch_comp
module branch_comp (
  input  [31:0] BrData1,
  input  [31:0] BrData2,
  input  BrUn,
  output BrEq,
  output BrLt
);

  wire and_1_out, and_2_out, and_3_out, and_4_out, comparator_1_eq, comparator_2_eq, comparator_3_lt,
       comparator_4_lt, not_1_out, not_2_out;

  Comparator #(.width(32)) comparator_1 (.a(BrData1), .b(BrData2), .eq(comparator_1_eq));  // open: gt, lt
  Comparator #(.mode("unsigned"), .width(32)) comparator_2 (
    .a(BrData1), .b(BrData2), .eq(comparator_2_eq));  // open: gt, lt
  Comparator #(.width(32)) comparator_3 (.a(BrData1), .b(BrData2), .lt(comparator_3_lt));  // open: gt, eq
  Comparator #(.mode("unsigned"), .width(32)) comparator_4 (
    .a(BrData1), .b(BrData2), .lt(comparator_4_lt));  // open: gt, eq
  not not_1 (not_1_out, BrUn);
  and and_1 (and_1_out, not_1_out, comparator_1_eq);
  and and_2 (and_2_out, BrUn, comparator_2_eq);
  not not_2 (not_2_out, BrUn);
  and and_3 (and_3_out, not_2_out, comparator_3_lt);
  and and_4 (and_4_out, BrUn, comparator_4_lt);
  or or_1 (BrEq, and_1_out, and_2_out);
  or or_2 (BrLt, and_3_out, and_4_out);

  // Notes on the sheet:
  //   BrUn Key:
  //   0 = signed comparison
  //   1 = unsigned comparison
  //   signed comparison
  //   signed comparison
  //   INPUTS to your circuit
  //   unsigned comparison
  //   unsigned comparison
  //   DON'T CHANGE THE LOCATIONS OF THE INPUTS AND OUTPUTS!
  //   BrEq = 1 iff values equal
  //   BrLt = 1 iff rs1 < rs2
  //   OUTPUT from your circuit
endmodule
