// Logisim project cpu.circ as structural Verilog: 1 circuit, main circuit cpu
module cpu (
  input  clk,
  input  [31:0] Instruction,
  input  [31:0] MemReadData,
  output [31:0] MemAddress,
  output [31:0] ProgramCounter,
  output [31:0] ra,
  output [31:0] sp,
  output [31:0] t0,
  output [31:0] t1,
  output [31:0] t2,
  output [31:0] s0,
  output [31:0] s1,
  output [31:0] a0,
  output [3:0] MemWriteMask,
  output [31:0] MemWriteData
);

  wire ASel, BrEq, BrLt, BrUn, BSel, comparator_1_eq, comparator_2_eq, imm7, imm20, imm31, MemWEn, PCSel,
       RegWEn, St_B_MemWEn, undriven_24, undriven_25, undriven_26, undriven_27, undriven_28, undriven_29,
       undriven_30, undriven_31, undriven_33, undriven_34, undriven_36, undriven_37, undriven_39,
       undriven_41, undriven_43, undriven_45, undriven_47, undriven_49, undriven_51, undriven_52,
       undriven_53, undriven_54, undriven_55, undriven_56, undriven_57, undriven_58, undriven_59,
       undriven_60, undriven_61, undriven_62, undriven_63, undriven_64, undriven_65, undriven_66,
       undriven_67, undriven_68, undriven_69, undriven_70, undriven_71, undriven_72, undriven_73,
       undriven_74, undriven_75, undriven_76, undriven_77, undriven_78, undriven_79, undriven_80,
       undriven_81, undriven_82, undriven_83, undriven_84, undriven_85, undriven_86;
  wire [1:0] undriven_87, undriven_88, undriven_89, undriven_90, undriven_91, undriven_92, undriven_93,
       undriven_94, undriven_95, WBSel;
  wire [2:0] format_simp;
  wire [3:0] ALUSel, Branch_format_alu, format, funct3_edit, I_format_alu, I_funct7, imm11_8, J_format_alu,
       R_format_alu, R_funct7_0x0, R_funct7_0x01, R_funct7_0x05, S_format_alu, U_format_alu, undriven,
       undriven_2, undriven_3, undriven_4, undriven_5, undriven_6, undriven_7, undriven_8, undriven_9,
       undriven_10, undriven_11, undriven_12, undriven_13, undriven_14, undriven_15, undriven_16,
       undriven_17, undriven_18, undriven_19, undriven_20, undriven_21, undriven_22, undriven_23,
       undriven_96, undriven_97, undriven_98;
  wire [4:0] branch_store_dest, destReg, imm11_7, multiplexer_6_out, S_format_dest, undriven_32, undriven_35,
       undriven_38, undriven_40, undriven_42, undriven_44, undriven_46, undriven_48, undriven_50;
  wire [5:0] imm30_25;
  wire [6:0] imm31_25;
  wire [7:0] imm19_12;
  wire [9:0] imm30_21;
  wire [10:0] imm31_12;
  wire [11:0] imm31_20;
  wire [31:0] adder_1_out, B, branch_store, BrData1, I_imm_math, I_load, J_jal, J_jalr, readReg1,
       RegWriteData, U_auipc, U_lui, val1, val2, val3, val6, val7, val9, val10, val11, val14, val15, val16,
       val17, val18, val19, val20, val21, val22, val23, val26, val28, val29, val30, val31;

  Register #(.width(32)) PC (.D(adder_1_out), .en(1'b1), .clk(clk), .Q(ProgramCounter));  // open: clr
  Adder #(.width(32)) adder_1 (.a(ProgramCounter), .b(32'h4), .out(adder_1_out));  // open: cin, cout
  // Probe on ProgramCounter
  // Probe on Instruction[24:20]
  // Probe on destReg
  // Probe on Instruction[19:15]
  // Probe on RegWriteData
  // Probe on RegWEn
  // Probe on Instruction
  // Probe on Instruction[6:2]
  // Probe on Instruction[14:12]
  // Probe on Instruction[31:25]
  // Probe on {Instruction[31], Instruction[25]}
  // Probe on Instruction[19:15]
  // Probe on Instruction[24:20]
  // Probe on Instruction[11:7]
  // Probe on imm31
  // Probe on imm31_25
  // Probe on imm31_12
  // Probe on imm31_20
  // Probe on imm30_25
  // Probe on imm30_21
  // Probe on imm20
  // Probe on imm19_12
  // Probe on imm11_8
  // Probe on imm11_7
  // Probe on imm7
  // Probe on format_simp
  control_logic control_logic_1 (
    .PCSel(PCSel), .RegWEn(RegWEn), .ImmSel(format_simp), .BrUn(BrUn), .ASel(ASel), .BSel(BSel),
    .ALUSel(ALUSel), .MemWEn(MemWEn), .WBSel(WBSel), .Instruction(Instruction), .BrEq(BrEq), .BrLt(BrLt));
  regfile regfile_1 (
    .ReadReg1(Instruction[19:15]), .ReadReg2(Instruction[24:20]), .WriteReg(destReg),
    .RegWriteData(RegWriteData), .RegWEn(RegWEn), .clk(clk), .ra(ra), .sp(sp), .t0(t0), .t1(t1), .t2(t2),
    .s0(s0), .s1(s1), .a0(a0), .RegReadData1(readReg1), .RegReadData2(branch_store));
  // Probe on branch_store
  // Probe on I_imm_math
  imm_gen imm_gen_1 (.Instruction(Instruction), .ImmSel(format_simp), .Immediate(I_imm_math));
  // Probe on readReg1
  Multiplexer #(.enable("false"), .select(5), .width(32)) multiplexer_1 (
    .in0(I_load), .in1(val1), .in2(val2), .in3(val3), .in4(I_imm_math), .in5(U_auipc), .in6(val6),
    .in7(val7), .in8(branch_store), .in9(val9), .in10(val10), .in11(val11), .in12(branch_store),
    .in13(U_lui), .in14(val14), .in15(val15), .in16(val16), .in17(val17), .in18(val18), .in19(val19),
    .in20(val20), .in21(val21), .in22(val22), .in23(val23), .in24(branch_store), .in25(J_jalr), .in26(val26),
    .in27(J_jal), .in28(val28), .in29(val29), .in30(val30), .in31(val31), .out(B), .sel(Instruction[6:2]));
  // Probe on readReg1
  // Probe on B
  // Probe on RegWriteData
  alu alu_1 (.ALUResult(RegWriteData), .A(readReg1), .B(B), .ALUSel(ALUSel));
  // Probe on ALUSel
  branch_comp branch_comp_1 (.BrData1(BrData1), .BrData2(BrData1), .BrUn(BrUn), .BrEq(BrEq), .BrLt(BrLt));
  Multiplexer #(.enable("false"), .select(5), .width(4)) multiplexer_2 (
    .in0(4'b0000), .in1(undriven), .in2(undriven_2), .in3(undriven_3), .in4(4'b0001), .in5(4'b0010),
    .in6(undriven_4), .in7(undriven_5), .in8(4'b0011), .in9(undriven_6), .in10(undriven_7),
    .in11(undriven_8), .in12(4'b0100), .in13(4'b0101), .in14(undriven_9), .in15(undriven_10),
    .in16(undriven_11), .in17(undriven_12), .in18(undriven_13), .in19(undriven_14), .in20(undriven_15),
    .in21(undriven_16), .in22(undriven_17), .in23(undriven_18), .in24(4'b1000), .in25(4'b0111),
    .in26(undriven_19), .in27(4'b0110), .in28(undriven_20), .in29(undriven_21), .in30(undriven_22),
    .in31(undriven_23), .out(format), .sel(Instruction[6:2]));
  // Probe on format
  // Probe on format
  Comparator #(.width(5)) comparator_1 (.a(Instruction[6:2]), .b(5'b01000), .eq(comparator_1_eq));  // open: gt, lt
  Comparator #(.width(3)) comparator_2 (.a(Instruction[14:12]), .b(3'b010), .eq(comparator_2_eq));  // open: gt, lt
  Multiplexer #(.enable("false"), .select(4)) multiplexer_3 (
    .in0(undriven_24), .in1(undriven_25), .in2(undriven_26), .in3(undriven_27), .in4(undriven_28),
    .in5(undriven_29), .in6(undriven_30), .in7(undriven_33), .in8(undriven_36), .out(BrEq), .sel(format));  // open: in9, in10, in11, in12, in13, in14, in15
  // Probe on destReg
  Multiplexer #(.enable("false"), .select(4), .width(5)) multiplexer_4 (
    .in0(Instruction[11:7]), .in1(Instruction[11:7]), .in2(Instruction[11:7]), .in3(S_format_dest),
    .in4(Instruction[11:7]), .in5(Instruction[11:7]), .in6(Instruction[11:7]), .in7(Instruction[11:7]),
    .in8(branch_store_dest), .out(destReg), .sel(format));  // open: in9, in10, in11, in12, in13, in14, in15
  // Probe on BrUn
  Multiplexer #(.enable("false"), .select(4)) multiplexer_5 (
    .in0(undriven_31), .in1(undriven_34), .in2(undriven_37), .in3(undriven_39), .in4(undriven_41),
    .in5(undriven_43), .in6(undriven_45), .in7(undriven_47), .in8(undriven_49), .out(BrUn), .sel(format));  // open: in9, in10, in11, in12, in13, in14, in15
  // Probe on multiplexer_6_out
  Multiplexer #(.enable("false"), .select(4), .width(5)) multiplexer_6 (
    .in0(undriven_32), .in1(undriven_35), .in2(undriven_38), .in3(undriven_40), .in4(undriven_42),
    .in5(undriven_44), .in6(undriven_46), .in7(undriven_48), .in8(undriven_50), .out(multiplexer_6_out),
    .sel(format));  // open: in9, in10, in11, in12, in13, in14, in15
  // Probe on BrEq
  partial_store partial_store_1 (
    .Instruction(Instruction), .MemAddress(MemAddress), .DataFromReg(readReg1), .MemWEn(MemWEn),
    .MemWriteMask(MemWriteMask), .DataToMem(ProgramCounter));
  partial_load partial_load_1 (
    .Instruction(Instruction), .MemAddress(MemAddress), .DataFromMem(Instruction), .DataToReg(RegWriteData));
  and and_1 (St_B_MemWEn, comparator_1_eq, comparator_2_eq);
  // Probe on BrLt
  Multiplexer #(.enable("false"), .select(4)) multiplexer_7 (
    .in0(undriven_51), .in1(undriven_52), .in2(undriven_53), .in3(undriven_54), .in4(undriven_55),
    .in5(undriven_56), .in6(undriven_57), .in7(undriven_58), .in8(undriven_59), .out(BrLt), .sel(format));  // open: in9, in10, in11, in12, in13, in14, in15
  Multiplexer #(.enable("false"), .select(4)) multiplexer_8 (
    .in0(undriven_60), .in1(undriven_61), .in2(undriven_62), .in3(undriven_63), .in4(undriven_64),
    .in5(undriven_65), .in6(undriven_66), .in7(undriven_67), .in8(undriven_68), .out(ASel), .sel(format));  // open: in9, in10, in11, in12, in13, in14, in15
  Multiplexer #(.enable("false"), .select(4)) multiplexer_9 (
    .in0(1'b0), .in1(1'b0), .in2(1'b0), .in3(1'b0), .in4(1'b0), .in5(1'b0), .in6(1'b0), .in7(1'b0),
    .in8(St_B_MemWEn), .out(MemWEn), .sel(format));  // open: in9, in10, in11, in12, in13, in14, in15
  // Probe on ASel
  // Probe on MemWEn
  Multiplexer #(.enable("false"), .select(4)) multiplexer_10 (
    .in0(undriven_69), .in1(undriven_70), .in2(undriven_71), .in3(undriven_72), .in4(undriven_73),
    .in5(undriven_74), .in6(undriven_76), .in7(undriven_78), .in8(undriven_80), .out(PCSel), .sel(format));  // open: in9, in10, in11, in12, in13, in14, in15
  // Probe on PCSel
  // Probe on BSel
  Multiplexer #(.enable("false"), .select(4)) multiplexer_11 (
    .in0(undriven_75), .in1(undriven_77), .in2(undriven_79), .in3(undriven_81), .in4(undriven_82),
    .in5(undriven_83), .in6(undriven_84), .in7(undriven_85), .in8(undriven_86), .out(BSel), .sel(format));  // open: in9, in10, in11, in12, in13, in14, in15
  // Probe on RegWEn
  Multiplexer #(.enable("false"), .select(4)) multiplexer_12 (
    .in0(1'b1), .in1(1'b1), .in2(1'b1), .in3(1'b0), .in4(1'b1), .in5(1'b1), .in6(1'b1), .in7(1'b1),
    .in8(1'b0), .out(RegWEn), .sel(format));  // open: in9, in10, in11, in12, in13, in14, in15
  // Probe on format_simp
  Multiplexer #(.enable("false"), .select(4), .width(3)) multiplexer_13 (
    .in0(3'b000), .in1(3'b000), .in2(3'b011), .in3(3'b001), .in4(3'b111), .in5(3'b011), .in6(3'b100),
    .in7(3'b100), .in8(3'b010), .out(format_simp), .sel(format));  // open: in9, in10, in11, in12, in13, in14, in15
  Multiplexer #(.enable("false"), .select(4), .width(4)) multiplexer_14 (
    .in0(funct3_edit), .in1(funct3_edit), .in2(funct3_edit), .in3(funct3_edit), .in4(funct3_edit),
    .in5(I_funct7), .in6(funct3_edit), .in7(funct3_edit), .in8(funct3_edit), .out(I_format_alu),
    .sel(funct3_edit));  // open: in9, in10, in11, in12, in13, in14, in15
  // Probe on WBSel
  Multiplexer #(.enable("false"), .select(4), .width(2)) multiplexer_15 (
    .in0(undriven_87), .in1(undriven_88), .in2(undriven_89), .in3(undriven_90), .in4(undriven_91),
    .in5(undriven_92), .in6(undriven_93), .in7(undriven_94), .in8(undriven_95), .out(WBSel), .sel(format));  // open: in9, in10, in11, in12, in13, in14, in15
  // Probe on I_format_alu
  Multiplexer #(.enable("false"), .select(2), .width(4)) multiplexer_16 (
    .in0(4'b0101), .in1(undriven_96), .in2(4'b1101), .out(I_funct7), .sel({Instruction[31], Instruction[25]}));  // open: in3
  assign funct3_edit = {{1{1'b0}}, Instruction[14:12]};  // Bit_Extender bit_extender_1
  Multiplexer #(.enable("false"), .select(4), .width(4)) multiplexer_17 (
    .in0(I_format_alu), .in1(I_format_alu), .in2(U_format_alu), .in3(S_format_alu), .in4(R_format_alu),
    .in5(U_format_alu), .in6(J_format_alu), .in7(J_format_alu), .in8(Branch_format_alu), .out(ALUSel),
    .sel(format));  // open: in9, in10, in11, in12, in13, in14, in15
  // Probe on I_funct7
  // Probe on ALUSel
  // Probe on R_format_alu
  Multiplexer #(.enable("false"), .select(4), .width(4)) multiplexer_18 (
    .in0(R_funct7_0x0), .in1(R_funct7_0x01), .in2(funct3_edit), .in3(funct3_edit), .in4(funct3_edit),
    .in5(R_funct7_0x05), .in6(funct3_edit), .in7(funct3_edit), .in8(funct3_edit), .out(R_format_alu),
    .sel(funct3_edit));  // open: in9, in10, in11, in12, in13, in14, in15
  // Probe on R_funct7_0x0
  Multiplexer #(.enable("false"), .select(2), .width(4)) multiplexer_19 (
    .in0(4'b0000), .in1(4'b1000), .in2(4'b1100), .out(R_funct7_0x0), .sel({Instruction[31], Instruction[25]}));  // open: in3
  Multiplexer #(.enable("false"), .select(2), .width(4)) multiplexer_20 (
    .in0(4'b0001), .in1(4'b1001), .in2(undriven_97), .out(R_funct7_0x01),
    .sel({Instruction[31], Instruction[25]}));  // open: in3
  // Probe on R_funct7_0x01
  // Probe on R_funct7_0x05
  Multiplexer #(.enable("false"), .select(2), .width(4)) multiplexer_21 (
    .in0(4'b0101), .in1(undriven_98), .in2(4'b1101), .out(R_funct7_0x05),
    .sel({Instruction[31], Instruction[25]}));  // open: in3

  // Other names for the same wires on the sheet: rs2[4:0] = Instruction[24:20]; funct7[6:0] = Instruction[31:25];
  //   ImmSel[2:0] = format_simp; funct3[2:0] = Instruction[14:12];
  //   funct7_edit[1:0] = {Instruction[31], Instruction[25]}; I_imm_math_dest[4:0] = Instruction[11:7];
  //   I_load_dest[4:0] = Instruction[11:7]; J_jal_dest[4:0] = Instruction[11:7]; J_jalr_dest[4:0] = Instruction[11:7];
  //   R_format_dest[4:0] = Instruction[11:7]; rd[4:0] = Instruction[11:7]; U_auipc_dest[4:0] = Instruction[11:7];
  //   U_lui_dest[4:0] = Instruction[11:7]; rs1[4:0] = Instruction[19:15]; opcode2_7[4:0] = Instruction[6:2];
  //   R_format[31:0] = branch_store; readReg2[31:0] = branch_store; S_format[31:0] = branch_store

  // Notes on the sheet:
  //   To IMEM
  //   IMEM (do **NOT** move this)
  //   From IMEM
  //   opcode
  //   funct3 (might have a problem being undefined)
  //   S-Format = 3
  //   These determine what values go to A, B
  //   Need to determine B for non I, R, S, Branch 
  //   Key:
  //   I-Fomat --> Load = 0
  //   I-Format --> imm log/arith = 1
  //   U-Format auipc = 2
  //   R-Format = 4
  //   U-Format lui = 5
  //   J-Formal jal = 6
  //   J-Format jalr = 7
  //   Branch / Store = 8
  //   Inputs/Outputs for testing. Do **NOT** move these.
  //   It is OK to move the PC, RegFile, ALU, MEM, Branch Comp, Imm Gen, Partial Load, Partial Store and Control Logic to wherever is most convenient for you when constructing your CPU, and to delete this text
  //   might be different for lw vs. sw
  //   always a register read value
  //   either a register read value or an immediate
  //   These These determine what format to use in with less overall values
  //   Opcodes:
  //   S-Format = 8
  //   still need to put RD for S, Branch
  //   R-Format: 12
  //   Branch / Store = 24
  //   J-Format --> jal: 27; jalr: 25
  //   U-Format --> lui = 13; auipc = 5
  //   I-Type --> immediate log/arith = 4; load = 0
  //   Opcodes:
  //   R-Format: 12
  //   S-Format = 8
  //   Branch / Store = 24
  //   J-Format --> jal: 27; jalr: 25
  //   U-Format --> lui = 13; auipc = 5
  //   This row has St_B_MemWEn; comparisons for Branch (BrData1, BrData2, BrUn, BrEq, BrLt)
  //   This row has BrUn, ASel, BSel, I_format_alu, I_funct7
  //   I-Type --> immediate log/arith = 4; load = 0
  //   This row has template, MemWEn, RegWEn, WBSel, funct7_edit
  //   and R_format_alu, R_funct7
  //   These determine what the return register is
  //   These determine
  //   still need to put RD for S, Branch
  //   This row has ImmSel, format_simp, ALUSel
  //   These determine
  //   To DMEM
  //   [Template]
  //   S-Format = 3
  //   R-Format = 4
  //   Key:
  //   I-Fomat --> Load = 0
  //   I-Format --> imm log/arith = 1
  //   U-Format auipc = 2
  //   S-Format = 3
  //   R-Format = 4
  //   U-Format lui = 5
  //   J-Formal jal = 6
  //   J-Format jalr = 7
  //   Branch / Store = 8
  //   DMEM (do **NOT** move this)
  //   Key:
  //   I-Fomat --> Load = 0
  //   I-Format --> imm log/arith = 1
  //   U-Format auipc = 2
  //   U-Format lui = 5
  //   J-Formal jal = 6
  //   J-Format jalr = 7
  //   Branch / Store = 8
  //   Key:
  //   I-Fomat --> Load = 0
  //   I-Format --> imm log/arith = 1
  //   U-Format auipc = 2
  //   S-Format = 3
  //   R-Format = 4
  //   U-Format lui = 5
  //   J-Formal jal = 6
  //   J-Format jalr = 7
  //   Branch / Store = 8
  //   Key:
  //   I-Fomat --> Load = 0
  //   I-Format --> imm log/arith = 1
  //   U-Format auipc = 2
  //   S-Format = 3
  //   R-Format = 4
  //   U-Format lui = 5
  //   J-Formal jal = 6
  //   J-Format jalr = 7
  //   Branch / Store = 8
  //   From DMEM
  //   These determine
  //   These determine
  //   These determine
  //   S-Format = 3
  //   R-Format = 4
  //   (assuming 0 = read; 1 = write)
  //   Key:
  //   I-Fomat --> Load = 0
  //   I-Format --> imm log/arith = 1
  //   U-Format auipc = 2
  //   U-Format lui = 5
  //   J-Formal jal = 6
  //   J-Format jalr = 7
  //   Branch / Store = 8
  //   I-Fomat --> Load = 0
  //   U-Format auipc = 2
  //   S-Format = 3
  //   R-Format = 4
  //   U-Format lui = 5
  //   J-Formal jal = 6
  //   J-Format jalr = 7
  //   Branch / Store = 8
  //   Key:
  //   I-Fomat --> Load = 0
  //   I-Format --> imm log/arith = 1
  //   U-Format auipc = 2
  //   S-Format = 3
  //   R-Format = 4
  //   U-Format lui = 5
  //   J-Formal jal = 6
  //   J-Format jalr = 7
  //   Branch / Store = 8
  //   Key:
  //   I-Format --> imm log/arith = 1
  //   These determine
  //   These determine
  //   These determine
  //   Key:
  //   I-Fomat --> Load = 0
  //   I-Format --> imm log/arith = 1
  //   U-Format auipc = 2
  //   S-Format = 3
  //   R-Format = 4
  //   U-Format lui = 5
  //   J-Formal jal = 6
  //   J-Format jalr = 7
  //   Branch / Store = 8
  //   S-Format = 3
  //   R-Format = 4
  //   S-Format = 3
  //   R-Format = 4
  //   Key:
  //   I-Fomat --> Load = 0
  //   I-Format --> imm log/arith = 1
  //   U-Format auipc = 2
  //   U-Format lui = 5
  //   J-Formal jal = 6
  //   J-Format jalr = 7
  //   Branch / Store = 8
  //   Key:
  //   I-Fomat --> Load = 0
  //   I-Format --> imm log/arith = 1
  //   U-Format auipc = 2
  //   U-Format lui = 5
  //   J-Formal jal = 6
  //   J-Format jalr = 7
  //   Branch / Store = 8
  //   These determine
  //   These determine
  //   These determine
  //   ImmSel Key:
  //   I-Format --> Load = 0 --> 0
  //   I-Format --> imm log/arith = 1 --> 0
  //   U-Format auipc = 2 --> 3
  //   S-Format = 3 --> 1
  //   R-Format = 4 --> n/a
  //   U-Format lui = 5 --> 3
  //   J-Formal jal = 6 --> 4
  //   J-Format jalr = 7 --> 4
  //   Branch / Store = 8 --> 2
  //   ALU Key:
  //   add = 0
  //   sll = 1
  //   slt = 2
  //   srl = 5
  //   xor = 4
  //   or = 6
  //   and = 7
  //   mul (sign) = 8
  //   mulh (sign) = 9
  //   mulhu = 11
  //   sub = 12
  //   sra = 13
  //   bsel = 15
  //   Key:
  //   I-Fomat --> Load = 0
  //   I-Format --> imm log/arith = 1
  //   U-Format auipc = 2
  //   S-Format = 3
  //   R-Format = 4
  //   U-Format lui = 5
  //   J-Formal jal = 6
  //   J-Format jalr = 7
  //   Branch / Store = 8
  //   use format to determine processing funct7 in conjunction with funct3
  //   Key:
  //   Note: funct_comb not yet defined
  //   0b0 --> 0x0
  //   0b10 = 2 --> 0x20
  //   0b01 = 1 --> 0x01
  //   I-Fomat --> Load = 0
  //   U-Format auipc = 2
  //   S-Format = 3
  //   R-Format = 4
  //   U-Format lui = 5
  //   J-Formal jal = 6
  //   J-Format jalr = 7
  //   Branch / Store = 8
  //   0 == 0 --> srl
  //   0b01 = 1 --> n/a
  //   0b10 = 2 --> sra
  //   can do addition for selection of item; use opcode as input; and output being funct_comb
  //   funct7 = 0, 0x20 (100000), or 0x01 (01) 
  //   only need to deal with only first and last bit
  //   Key:
  //   I-Format --> imm log/arith = 1
  //   These determine
  //   ALU Key:
  //   add = 0
  //   sll = 1
  //   slt = 2
  //   srl = 5
  //   xor = 4
  //   or = 6
  //   and = 7
  //   sub = 12
  //   sra = 13
  //   bsel = 15
  //   mul (sign) = 8
  //   mulh (sign) = 9
  //   mulhu = 11
  //   special branches: 0 (3), 1 (2), 5 (2)
  //   Key:
  //   0b0 = 0 --> add
  //   0b01 = 1 --> mul
  //   0b10 = 2 --> sub
  //   Key:
  //   0b0 = 0 --> sll
  //   TODO: put correct bottom values for R_funct7_0x##
  //   0b01 = 1 --> mulh
  //   0b10 = 2 --> n/a
  //   ALU Key:
  //   add = 0
  //   sll = 1
  //   slt = 2
  //   srl = 5
  //   xor = 4
  //   or = 6
  //   and = 7
  //   mul (sign) = 8
  //   mulh (sign) = 9
  //   mulhu = 11
  //   sub = 12
  //   sra = 13
  //   bsel = 15
  //   Key:
  //   0b0 = 0 --> srl
  //   0b01 = 1 --> n/a
  //   0b10 = 2 --> sra
endmodule
