// Logisim project imm-gen.circ as structural Verilog: 1 circuit, main circuit imm_gen
module imm_gen (
  input  [31:0] Instruction,
  input  [2:0] ImmSel,
  output [31:0] Immediate
);

  wire and_1_out, comparator_1_eq, comparator_2_eq, comparator_3_eq, comparator_4_eq, comparator_5_eq,
       comparator_6_eq, comparator_7_eq, comparator_8_eq, comparator_9_eq, comparator_10_eq, not_1_out,
       not_2_out, or_1_out, or_2_out, or_3_out, or_4_out, or_5_out;
  wire [31:0] and_2_out, and_3_out, and_4_out, bit_extender_1_out, bit_extender_2_out, bit_extender_6_out,
       bit_extender_7_out, bit_extender_8_out, Branch_imm, I_imm, J_imm, S_imm;

  assign bit_extender_1_out = {{20{Instruction[31]}}, Instruction[31:20]};  // Bit_Extender bit_extender_1
  Comparator #(.mode("unsigned"), .width(5)) comparator_1 (
    .a(Instruction[6:2]), .b(5'b00100), .eq(comparator_1_eq));  // open: gt, lt
  Comparator #(.mode("unsigned"), .width(3)) comparator_2 (
    .a(Instruction[14:12]), .b(3'b001), .eq(comparator_2_eq));  // open: gt, lt
  Comparator #(.mode("unsigned"), .width(3)) comparator_3 (
    .a(Instruction[14:12]), .b(3'b101), .eq(comparator_3_eq));  // open: gt, lt
  assign bit_extender_2_out = {{27{1'b0}}, Instruction[24:20]};  // Bit_Extender bit_extender_2
  Comparator #(.mode("unsigned"), .width(3)) comparator_4 (
    .a(Instruction[14:12]), .b(3'b001), .eq(comparator_4_eq));  // open: gt, lt
  Comparator #(.mode("unsigned"), .width(3)) comparator_5 (
    .a(Instruction[14:12]), .b(3'b101), .eq(comparator_5_eq));  // open: gt, lt
  Comparator #(.mode("unsigned"), .width(5)) comparator_6 (
    .a(Instruction[6:2]), .b(5'b00100), .eq(comparator_6_eq));  // open: gt, lt
  or or_1 (or_1_out, comparator_2_eq, comparator_3_eq);
  not not_1 (not_1_out, or_1_out);
  or or_2 (or_2_out, comparator_4_eq, comparator_5_eq);
  assign S_imm = {{20{Instruction[31]}}, {Instruction[31:25], Instruction[11:7]}};  // Bit_Extender bit_extender_3
  assign Branch_imm = {{19{Instruction[31]}}, {Instruction[31], Instruction[7], Instruction[30:25], Instruction[11:8], 1'b0}};  // Bit_Extender bit_extender_4
  assign J_imm = {{11{Instruction[31]}}, {Instruction[31], Instruction[19:12], Instruction[20], Instruction[30:21], 1'b0}};  // Bit_Extender bit_extender_5
  Comparator #(.mode("unsigned"), .width(3)) comparator_7 (
    .a(Instruction[14:12]), .b(3'b001), .eq(comparator_7_eq));  // open: gt, lt
  Comparator #(.mode("unsigned"), .width(3)) comparator_8 (
    .a(Instruction[14:12]), .b(3'b101), .eq(comparator_8_eq));  // open: gt, lt
  and and_1 (and_1_out, comparator_1_eq, not_1_out);
  Comparator #(.mode("unsigned"), .width(5)) comparator_9 (
    .a(Instruction[6:2]), .b({5{1'b0}}), .eq(comparator_9_eq));  // open: gt, lt
  Comparator #(.mode("unsigned"), .width(5)) comparator_10 (
    .a(Instruction[6:2]), .b(5'b11001), .eq(comparator_10_eq));  // open: gt, lt
  assign bit_extender_6_out = {{31{or_2_out}}, or_2_out};  // Bit_Extender bit_extender_6
  assign bit_extender_7_out = {{31{comparator_6_eq}}, comparator_6_eq};  // Bit_Extender bit_extender_7
  or or_3 (or_3_out, comparator_7_eq, comparator_8_eq);
  not not_2 (not_2_out, or_3_out);
  assign bit_extender_8_out = {{31{or_4_out}}, or_4_out};  // Bit_Extender bit_extender_8
  or or_4 (or_4_out, and_1_out, or_5_out);
  or or_5 (or_5_out, comparator_9_eq, comparator_10_eq);
  assign and_2_out = bit_extender_2_out & and_3_out;  // AND_Gate and_2, 32 bits wide
  assign and_3_out = bit_extender_6_out & bit_extender_7_out;  // AND_Gate and_3, 32 bits wide
  Bit_Extender #(.in_width(1), .out_width(32)) bit_extender_9 (.in(not_2_out));  // open: out
  assign and_4_out = bit_extender_1_out & bit_extender_8_out;  // AND_Gate and_4, 32 bits wide
  assign I_imm = and_4_out | and_2_out;  // OR_Gate or_6, 32 bits wide
  // Probe on 32'h13
  // Probe on I_imm
  // Probe on I_imm
  // Probe on Immediate
  Multiplexer #(.enable("false"), .select(3), .width(32)) multiplexer_1 (
    .in0(I_imm), .in1(S_imm), .in2(Branch_imm), .in3({Instruction[31:12], {12{1'b0}}}), .in4(J_imm),
    .out(Immediate), .sel(ImmSel));  // open: in5, in6, in7

  // Other names for the same wires on the sheet: funct3[2:0] = Instruction[14:12]; imm19_12[7:0] = Instruction[19:12];
  //   imm31_12[19:0] = Instruction[31:12]; U_imm[31:12] = Instruction[31:12]; imm4_0[4:0] = Instruction[11:7];
  //   imm11_b = Instruction[7]; imm4_1[3:0] = Instruction[11:8]; imm10_1[9:0] = Instruction[30:21];
  //   imm10_5[5:0] = Instruction[30:25]; imm11_0[11:0] = Instruction[31:20]; imm11_5[6:0] = Instruction[31:25];
  //   imm12_b = Instruction[31]; imm20_j = Instruction[31]; imm11_j = Instruction[20];
  //   shamt[4:0] = Instruction[24:20]; opcode2_6[4:0] = Instruction[6:2]

  // Notes on the sheet:
  //   INPUTS to your circuit
  //   I-Format arithmetic
  //   want 31-20
  //   I don't know what to bit for bit 0; leaving it as 0
  //   I*
  //   note that this is 0-extended because I'm not quite sure what to do here :)
  //   ImmSel Key:
  //   I-Format = 0
  //   S-Format = 1
  //   Branch-Format = 2
  //   U-Format = 3
  //   J-Format = 4
  //   b6-7
  //   20-25
  //   b31-20
  //   26-31
  //   imm[11:0], 31-20
  //   Load instructions a little complicated (I-format)
  //   note that this is 0-extended because I'm not quite sure what to do here :)
  //   This circuit generates immediates
  //   b7
  //   imm11_0 indicates what position in array
  //   25
  //   I-Format
  //   S-Format
  //   Branch-Format
  //   J-Format
  //   U-Format
  //   DON'T CHANGE THE LOCATIONS OF THE INPUTS AND OUTPUTS!
  //   undefined
  //   ImmSel Key:
  //   I-Format = 0
  //   S-Format = 1
  //   need to still account for shift immediate (I-Format) actions w/ opcode & funct3
  //   OUTPUT from your circuit
  //   Branch-Format = 2
  //   U-Format = 3
  //   J-Format = 4
endmodule
