// Logisim project partial-load.circ as structural Verilog: 1 circuit, main circuit partial_load
module partial_load (
  input  [31:0] Instruction,
  input  [31:0] MemAddress,
  input  [31:0] DataFromMem,
  output [31:0] DataToReg
);

  wire [31:0] lb_0, lb_1, lb_2, lb_3, lh_4, lh_5, lh_6;

  assign lb_0 = {{24{DataFromMem[7]}}, DataFromMem[7:0]};  // Bit_Extender bit_extender_1
  assign lb_1 = {{24{DataFromMem[15]}}, DataFromMem[15:8]};  // Bit_Extender bit_extender_2
  assign lb_2 = {{24{DataFromMem[23]}}, DataFromMem[23:16]};  // Bit_Extender bit_extender_3
  assign lb_3 = {{24{DataFromMem[31]}}, DataFromMem[31:24]};  // Bit_Extender bit_extender_4
  assign lh_4 = {{16{DataFromMem[15]}}, DataFromMem[15:0]};  // Bit_Extender bit_extender_5
  assign lh_6 = {{16{DataFromMem[31]}}, DataFromMem[31:16]};  // Bit_Extender bit_extender_6
  assign lh_5 = {{16{DataFromMem[23]}}, DataFromMem[23:8]};  // Bit_Extender bit_extender_7
  Multiplexer #(.enable("false"), .select(4), .width(32)) multiplexer_1 (
    .in0(lb_0), .in1(lb_1), .in2(lb_2), .in3(lb_3), .in4(lh_4), .in5(lh_5), .in6(lh_6), .in8(DataFromMem),
    .out(DataToReg), .sel({Instruction[13:12], MemAddress[31:30]}));  // open: in7, in9, in10, in11, in12, in13, in14, in15

  // Other names for the same wires on the sheet: bottom_MemAddress[1:0] = MemAddress[31:30];
  //   LoadSel[3:0] = {Instruction[13:12], MemAddress[31:30]}; funct3_13_12[1:0] = Instruction[13:12]

  // Notes on the sheet:
  //   INPUTS to your circuit
  //   1) set up logic to determine whether lw (32), lh (16), or lb (8) --> sign extend to 32 before returning 
  //   Key:
  //   lb:
  //   lh:
  //   lw:
  //   0b1000 = 8
  //   0b0000 = 0
  //   0b0001 = 1
  //   0b0010 = 2
  //   0b0011 = 3
  //   0b0100 = 4
  //   0b0101 = 5
  //   0b0110 = 6
  //   DON'T CHANGE THE LOCATIONS OF THE INPUTS AND OUTPUTS!
  //   OUTPUT from your circuit
endmodule
