// Logisim project partial-store.circ as structural Verilog: 1 circuit, main circuit partial_store
module partial_store (
  input  [31:0] Instruction,
  input  [31:0] MemAddress,
  input  [31:0] DataFromReg,
  input  MemWEn,
  output [3:0] MemWriteMask,
  output [31:0] DataToMem
);

  wire [3:0] bit_extender_1_out, multiplexer_1_out;

  // Probe on 4'b0001
  // Probe on 4'b0010
  // Probe on 4'b0100
  // Probe on 4'b1000
  // Probe on 4'b0011
  // Probe on 4'b1100
  // Probe on 4'b1111
  assign bit_extender_1_out = {{3{MemWEn}}, MemWEn};  // Bit_Extender bit_extender_1
  Multiplexer #(.enable("false"), .select(4), .width(4)) multiplexer_1 (
    .in0(4'b0001), .in1(4'b0010), .in2(4'b0100), .in3(4'b1000), .in4(4'b0011), .in6(4'b1100), .in8(4'b1111),
    .out(multiplexer_1_out), .sel({Instruction[13:12], MemAddress[1:0]}));  // open: in5, in7, in9, in10, in11, in12, in13, in14, in15
  assign MemWriteMask = bit_extender_1_out & multiplexer_1_out;  // AND_Gate and_1, 4 bits wide
  Multiplexer #(.enable("false"), .select(4), .width(32)) multiplexer_2 (
    .in0({{24{1'b0}}, DataFromReg[7:0]}), .in1({{16{1'b0}}, DataFromReg[7:0], {8{1'b0}}}),
    .in2({{8{1'b0}}, DataFromReg[7:0], {16{1'b0}}}), .in3({DataFromReg[7:0], {24{1'b0}}}),
    .in4({{16{1'b0}}, DataFromReg[15:0]}), .in6({DataFromReg[15:0], {16{1'b0}}}), .in8(DataFromReg),
    .out(DataToMem), .sel({Instruction[13:12], MemAddress[1:0]}));  // open: in5, in7, in9, in10, in11, in12, in13, in14, in15

  // Other names for the same wires on the sheet: sb[7:0] = DataFromReg[7:0]; sh[15:0] = DataFromReg[15:0];
  //   sw[31:0] = DataFromReg; bottom_MemAddress[1:0] = MemAddress[1:0];
  //   MaskSel[3:0] = {Instruction[13:12], MemAddress[1:0]}; funct3_13_12[1:0] = Instruction[13:12]

  // Notes on the sheet:
  //   INPUTS to your circuit
  //   pass 32 bit address to DMEM to get bytes starting at that address
  //   all memory accesses need to be aligned (16, 17, 18, 19)
  //   bits 1-0 or 31-30
  //   dmem able to access 4 bytes at a time; start at address that is a multiple of 4
  //   memory unit can only use lower 16 bits of provided address due to Logism limits
  //   lw and sw instructions will use memory addresses ending in 0b###00 (multiple of 4)
  //   lh sh use memory addresses ending in 0b##00, 0b##01, 0b##10; never 0b##11
  //   provided address rounded out to nearest multiple of 4 due to DMEM zeroing out last 2 bits of provided address
  //   Key:
  //   sb:
  //   sb:
  //   sw:
  //   0b0000 = 0 --> m = 0b0001 = 1
  //   0b0001 = 1 --> m = 0b0010 = 2
  //   0b0010 = 2--> m = 0b0100 = 4
  //   0b0011 = 3 --> m = 0b1000 = 8
  //   0b0100 = 4 --> m = 0b0011 = 3
  //   0b0110 = 6 --> m = 0b1100 = 12
  //   0b1000 = 8 --> m = 0b1111 = 15
  //   DON'T CHANGE THE LOCATIONS OF THE INPUTS AND OUTPUTS!
  //   OUTPUT from your circuit
endmodule
