// Logisim project regfile.circ as structural Verilog: 1 circuit, main circuit regfile
module regfile (
  input  [4:0] ReadReg1,
  input  [4:0] ReadReg2,
  input  [4:0] WriteReg,
  input  [31:0] RegWriteData,
  input  RegWEn,
  input  clk,
  output [31:0] ra,
  output [31:0] sp,
  output [31:0] t0,
  output [31:0] t1,
  output [31:0] t2,
  output [31:0] s0,
  output [31:0] s1,
  output [31:0] a0,
  output [31:0] RegReadData1,
  output [31:0] RegReadData2
);

  wire x1, x2, x3, x4, x5, x6, x7, x8, x9, x10, x11, x12, x13, x14, x15, x16, x17, x18, x19, x20, x21, x22,
       x23, x24, x25, x26, x27, x28, x29, x30, x31;
  wire [4:0] bit_extender_1_out, bit_extender_2_out, multiplier_1_out, multiplier_2_out;
  wire [31:0] rx0, rx3, rx4, rx11, rx12, rx13, rx14, rx15, rx16, rx17, rx18, rx19, rx20, rx21, rx22, rx23,
       rx24, rx25, rx26, rx27, rx28, rx29, rx30, rx31;

  assign bit_extender_1_out = {{4{1'b0}}, RegWEn};  // Bit_Extender bit_extender_1
  Multiplier #(.width(5)) multiplier_1 (
    .a(WriteReg), .b(bit_extender_1_out), .out(multiplier_1_out));  // open: cin, cout
  Demultiplexer #(.enable("false"), .select(5)) demultiplexer_1 (
    .out1(x1), .out2(x2), .out3(x3), .out4(x4), .out5(x5), .out6(x6), .out7(x7), .out8(x8), .out9(x9),
    .out10(x10), .out11(x11), .out12(x12), .out13(x13), .out14(x14), .out15(x15), .out16(x16), .out17(x17),
    .out18(x18), .out19(x19), .out20(x20), .out21(x21), .out22(x22), .out23(x23), .out24(x24), .out25(x25),
    .out26(x26), .out27(x27), .out28(x28), .out29(x29), .out30(x30), .out31(x31), .in(RegWEn),
    .sel(multiplier_1_out));  // open: out0
  Multiplexer #(.enable("false"), .select(5), .width(32)) multiplexer_1 (
    .in0(rx0), .in1(ra), .in2(sp), .in3(rx3), .in4(rx4), .in5(t0), .in6(t1), .in7(t2), .in8(s0), .in9(s1),
    .in10(a0), .in11(rx11), .in12(rx12), .in13(rx13), .in14(rx14), .in15(rx15), .in16(rx16), .in17(rx17),
    .in18(rx18), .in19(rx19), .in20(rx20), .in21(rx21), .in22(rx22), .in23(rx23), .in24(rx24), .in25(rx25),
    .in26(rx26), .in27(rx27), .in28(rx28), .in29(rx29), .in30(rx30), .in31(rx31), .out(RegReadData1),
    .sel(ReadReg1));
  Multiplexer #(.enable("false"), .select(5), .width(32)) multiplexer_2 (
    .in0(rx0), .in1(ra), .in2(sp), .in3(rx3), .in4(rx4), .in5(t0), .in6(t1), .in7(t2), .in8(s0), .in9(s1),
    .in10(a0), .in11(rx11), .in12(rx12), .in13(rx13), .in14(rx14), .in15(rx15), .in16(rx16), .in17(rx17),
    .in18(rx18), .in19(rx19), .in20(rx20), .in21(rx21), .in22(rx22), .in23(rx23), .in24(rx24), .in25(rx25),
    .in26(rx26), .in27(rx27), .in28(rx28), .in29(rx29), .in30(rx30), .in31(rx31), .out(RegReadData2),
    .sel(ReadReg2));
  Register #(.width(32)) x0 (.D({32{1'b0}}), .en(1'b0), .clk(clk), .Q(rx0));  // open: clr
  Register #(.width(32)) u_x6 (.D(RegWriteData), .en(x6), .clk(clk), .Q(t1));  // open: clr
  Register #(.width(32)) u_x12 (.D(RegWriteData), .en(x12), .clk(clk), .Q(rx12));  // open: clr
  Register #(.width(32)) u_x18 (.D(RegWriteData), .en(x18), .clk(clk), .Q(rx18));  // open: clr
  Register #(.width(32)) u_x24 (.D(RegWriteData), .en(x24), .clk(clk), .Q(rx24));  // open: clr
  Register #(.width(32)) u_x30 (.D(RegWriteData), .en(x30), .clk(clk), .Q(rx30));  // open: clr
  Register #(.width(32)) u_x1 (.D(RegWriteData), .en(x1), .clk(clk), .Q(ra));  // open: clr
  Register #(.width(32)) u_x7 (.D(RegWriteData), .en(x7), .clk(clk), .Q(t2));  // open: clr
  Register #(.width(32)) u_x13 (.D(RegWriteData), .en(x13), .clk(clk), .Q(rx13));  // open: clr
  Register #(.width(32)) u_x19 (.D(RegWriteData), .en(x19), .clk(clk), .Q(rx19));  // open: clr
  Register #(.width(32)) u_x25 (.D(RegWriteData), .en(x25), .clk(clk), .Q(rx25));  // open: clr
  Register #(.width(32)) u_x31 (.D(RegWriteData), .en(x31), .clk(clk), .Q(rx31));  // open: clr
  assign bit_extender_2_out = {{4{1'b0}}, RegWEn};  // Bit_Extender bit_extender_2
  BitSelector #(.group(5), .width(5)) bitselector_1 (.in(multiplier_2_out));  // open: out, sel
  Multiplier #(.width(5)) multiplier_2 (
    .a(WriteReg), .b(bit_extender_2_out), .out(multiplier_2_out));  // open: cin, cout
  Register #(.width(32)) u_x2 (.D(RegWriteData), .en(x2), .clk(clk), .Q(sp));  // open: clr
  Register #(.width(32)) u_x8 (.D(RegWriteData), .en(x8), .clk(clk), .Q(s0));  // open: clr
  Register #(.width(32)) u_x14 (.D(RegWriteData), .en(x14), .clk(clk), .Q(rx14));  // open: clr
  Register #(.width(32)) u_x20 (.D(RegWriteData), .en(x20), .clk(clk), .Q(rx20));  // open: clr
  Register #(.width(32)) u_x26 (.D(RegWriteData), .en(x26), .clk(clk), .Q(rx26));  // open: clr
  Register #(.width(32)) u_x3 (.D(RegWriteData), .en(x3), .clk(clk), .Q(rx3));  // open: clr
  Register #(.width(32)) u_x9 (.D(RegWriteData), .en(x9), .clk(clk), .Q(s1));  // open: clr
  Register #(.width(32)) u_x15 (.D(RegWriteData), .en(x15), .clk(clk), .Q(rx15));  // open: clr
  Register #(.width(32)) u_x21 (.D(RegWriteData), .en(x21), .clk(clk), .Q(rx21));  // open: clr
  Register #(.width(32)) u_x27 (.D(RegWriteData), .en(x27), .clk(clk), .Q(rx27));  // open: clr
  Register #(.width(32)) u_x4 (.D(RegWriteData), .en(x4), .clk(clk), .Q(rx4));  // open: clr
  Register #(.width(32)) u_x10 (.D(RegWriteData), .en(x10), .clk(clk), .Q(a0));  // open: clr
  Register #(.width(32)) u_x16 (.en(x16), .clk(clk), .Q(rx16));  // open: D, clr
  Register #(.width(32)) u_x22 (.D(RegWriteData), .en(x22), .clk(clk), .Q(rx22));  // open: clr
  Register #(.width(32)) u_x28 (.D(RegWriteData), .en(x28), .clk(clk), .Q(rx28));  // open: clr
  Register #(.width(32)) u_x5 (.D(RegWriteData), .en(x5), .clk(clk), .Q(t0));  // open: clr
  Register #(.width(32)) u_x11 (.D(RegWriteData), .en(x11), .clk(clk), .Q(rx11));  // open: clr
  Register #(.width(32)) u_x17 (.D(RegWriteData), .en(x17), .clk(clk), .Q(rx17));  // open: clr
  Register #(.width(32)) u_x23 (.D(RegWriteData), .en(x23), .clk(clk), .Q(rx23));  // open: clr
  Register #(.width(32)) u_x29 (.D(RegWriteData), .en(x29), .clk(clk), .Q(rx29));  // open: clr

  // Other names for the same wires on the sheet: rx1[31:0] = ra; rx2[31:0] = sp; rx5[31:0] = t0; rx6[31:0] = t1;
  //   rx7[31:0] = t2; rx8[31:0] = s0; rx9[31:0] = s1; rx10[31:0] = a0

  // Notes on the sheet:
  //   writes 1 to selected register
  //   0 otherwise
  //   INPUTS to your circuit
  //   Q is output
  //   R is signal
  //   D leads to input
  //   WE is write-enable
  //   TODO: Complete ReadRegisters & test Task 2
  //   since decoders only take inputs with bit width 1, need to split up groups
  //   connect rx# registers to correct element (muliplexor? demultiplexor? decoder? for ReadRegisters)
  //   DON'T CHANGE THE LOCATIONS OF THE INPUTS AND OUTPUTS!
  //   These are DEBUG/TEST outputs from your circuit.
  //   OUTPUTS from your circuit
endmodule
